# Fritzing sketch pool-controller (saved by Fritzing 0.9.3b)
circuit board: 5.92561cm x 5.10948cm
breadboards: 1

parts:
  U1 = NodeMCU V1.0
  R1 = Resistor [tolerance=±5% resistance=4.7k package=THT]
  DS2_(Water) = DS18B20 1-Wire Temperature Sensor Probe Cable
  R2 = Resistor [tolerance=±5% resistance=4.7k package=THT]
  DS3_(Solar) = DS18B20 1-Wire Temperature Sensor Probe Cable
  U2 = Module 4 Relais 5V [package="Module 4 Relais 5V"]

nets:
  N1: U1.D1, U2.IN1
  N2: U1.D2, U2.IN2
  VDD: U1.3V3, R1.Pin_0, DS2_(Water).VDD, R2.Pin_0, DS3_(Solar).VDD
  GND: U1.GND, DS2_(Water).GND, DS3_(Solar).GND, U2.GND
  N3: U1.D5, R2.Pin_1, DS3_(Solar).DQ
  N4: U1.D6, R1.Pin_1, DS2_(Water).DQ
  VIN: U1.Vin, U2.VCC

notes:
  Smart Swimmingpool Controller
  Pool-Pump
  Solar-Pump

custom parts:
  NodeMCU V1.0: ESP8266 based NodeMCU
  Module 4 Relais 5V: Module 4 Relais 5V 4x SPD-06VDC-SD-C
